# Fritzing sketch Rangkaian Eletronik (saved by Fritzing 0.9.3b)

parts:
  Part1 = Soil Moisture Sensor
  Part4 = Arduino Uno (Rev3) - ICSP
  Part5 = Arduino Uno (Rev3) - ICSP
  VCC1 = Battery block 9V  # not connected
  RS485_module1 = RS485 Module (MAX3485)
  U1 = 2-Channel 5v Relay Shield [package=relay-2ch5v10a]
  Part6 = Arduino Uno (Rev3) - ICSP
  VCC2 = Battery block 9V
  M2 = DC Motor
  VCC3 = Battery block 9V
  M1 = DC Motor
  Part7 = Arduino Uno (Rev3) - ICSP  # not connected

nets:
  N1: Part1.SIG, Part4.A0
  GND: Part1.GND, Part4.GND
  VCC: Part1.VCC, Part4.5V
  N2: Part5.D8, RS485_module1.RE
  N3: Part5.D2, RS485_module1.RO
  N4: Part5.D3_PWM, RS485_module1.DI
  N5: Part5.D7, RS485_module1.DE
  VCC_2: U1.VCC, Part6.5V
  GND_2: U1.GND, Part6.GND
  N6: U1.IN1, Part6.D4
  N7: U1.IN2, Part6.D5_PWM
  N8: U1.K1-In, VCC3.+
  N9: U1.K1-On, M2.pin_1
  N10: U1.K2-In, VCC2.+
  N11: U1.K2-On, M1.pin_1

notes:
  Arduino Wemos D1
  Sensor Moisture Soil

custom parts:
  RS485 Module (MAX3485): Commercially available RS485 to RS232 TTL Module
  2-Channel 5v Relay Shield: 2 Channel 5v Relay Shield w. 2x SPD-06VDC-SD-C
